// Logisim project circuit.circ as structural Verilog: 2 circuits, main circuit main
module main (
  input  in_1,
  input  in_2,
  input  in_3,
  input  in_4,
  input  in_5,
  input  in_6,
  input  in_7,
  input  in_8,
  input  in_9,
  input  in_10,
  input  in_11,
  input  in_12,
  input  in_13,
  input  in_14,
  input  in_15,
  input  in_16,
  output isMOV
);

  wire and_1_out, and_2_out, and_3_out, and_4_out, and_5_out, and_6_out, and_7_out, and_8_out, and_9_out,
       and_10_out, and_11_out, and_12_out, and_13_out, and_14_out;

  and and_1 (and_1_out, in_1, in_2);
  and and_2 (and_2_out, in_3, in_4);
  and and_3 (and_3_out, in_5, in_6);
  and and_4 (and_4_out, in_7, in_8);
  and and_5 (and_5_out, in_9, in_10);
  and and_6 (and_6_out, in_11, in_12);
  and and_7 (and_7_out, in_13, in_14);
  and and_8 (and_8_out, in_15, in_16);
  and and_9 (and_9_out, and_1_out, and_2_out);
  and and_10 (and_10_out, and_3_out, and_4_out);
  and and_11 (and_11_out, and_5_out, and_6_out);
  and and_12 (and_12_out, and_7_out, and_8_out);
  and and_13 (and_13_out, and_9_out, and_10_out);
  and and_14 (and_14_out, and_11_out, and_12_out);
  and and_15 (isMOV, and_13_out, and_14_out);
endmodule

module InstructionDeterminer (
  input  ib1,
  input  ib2,
  input  ib3,
  input  ib4,
  input  ib5,
  input  ib6,
  input  ib7,
  input  ib8,
  input  ib9,
  input  ib10,
  input  ib11,
  input  ib12,
  input  ib13,
  input  ib14,
  input  ib15,
  input  ib16,
  output isMOV
);

  wire and_1_out, and_2_out, and_3_out, and_4_out, and_5_out, and_6_out, and_7_out, and_8_out, and_9_out,
       and_10_out, and_11_out, and_12_out, and_13_out, and_14_out;

  and and_1 (and_1_out, ib1, ib2);
  and and_2 (and_2_out, ib3, ib4);
  and and_3 (and_3_out, ib5, ib6);
  and and_4 (and_4_out, ib7, ib8);
  and and_5 (and_5_out, ib9, ib10);
  and and_6 (and_6_out, ib11, ib12);
  and and_7 (and_7_out, ib13, ib14);
  and and_8 (and_8_out, ib15, ib16);
  and and_9 (and_9_out, and_1_out, and_2_out);
  and and_10 (and_10_out, and_3_out, and_4_out);
  and and_11 (and_11_out, and_5_out, and_6_out);
  and and_12 (and_12_out, and_7_out, and_8_out);
  and and_13 (and_13_out, and_9_out, and_10_out);
  and and_14 (and_14_out, and_11_out, and_12_out);
  and and_15 (isMOV, and_13_out, and_14_out);

  // Other names for the same wires on the sheet: cb1 = ib1; cb2 = ib2; cb3 = ib3; cb4 = ib4; cb5 = ib5; cb6 = ib6;
  //   cb7 = ib7; cb8 = ib8; cb9 = ib9; cb10 = ib10; cb11 = ib11; cb12 = ib12; cb13 = ib13; cb14 = ib14; cb15 = ib15;
  //   cb16 = ib16
endmodule
